# Fritzing sketch Motor-controller-sketch (saved by Fritzing 0.9.5d)
breadboards: 1

parts:
  Part1 = Arduino Uno (Rev3)
  R1 = Trimmer Potentiometer [maximum_resistance=10kΩ package=THT]
  R2 = Resistor [tolerance=±5% resistance=220 package=THT]
  LED1 = LED - 5mm [color="Red (633nm)" package="5 mm [THT]"]
  LED2 = LED - 5mm [color="Red (633nm)" package="5 mm [THT]"]
  M1 = DC Motor
  IC1 = L293D [package=THT]
  S1 = Momentary Switch [package=ksa_sealed_tac_switch]
  R3 = Resistor [tolerance=±5% resistance=220 package=THT]
  LED3 = LED - 5mm [color="Red (633nm)" package="5 mm [THT]"]
  R4 = Resistor [tolerance=±5% resistance=220 package=THT]

nets:
  N1: Part1.A0, R1.wiper, LED3.anode
  N2: Part1.D10_PWM/SS, IC1.Enable_1
  N3: Part1.D11_PWM/MOSI, IC1.In_1
  N4: Part1.D12/MISO, IC1.In_2
  N5: Part1.D13/SCK, S1.4, R3.Pin_0
  N6: Part1.GND, R1.leg1, IC1.0V, R3.Pin_1, R4.Pin_0
  N7: Part1.5V, R1.leg2, IC1.+V, S1.2
  N8: R2.Pin_0, M1.pin_2, IC1.Out_1_(_Controlled_by_Enable_1_)
  N9: LED1.cathode, LED2.anode
  N10: LED1.anode, LED2.cathode, M1.pin_1, IC1.Out_2_(_Controlled_by_Enable_1_)
  N11: LED3.cathode, R4.Pin_1
